# Fritzing sketch schematic2_ftizing (saved by Fritzing 0.9.3b)

parts:
  MAX30102_Sensor1 = MAX30102 Oximeter and Heart-Rate Sensor [part_number=MAX30102]
  A1 = usbc to 12V module
  SG1 = Buzzer 12mm [package=buzzer-12mm]
  LED1 = smd LED [color="Red (633nm)" package="0805 [SMD]"]
  LED2 = smd LED [color="Green (570nm)" package="0805 [SMD]"]
  R1 = Resistor [tolerance=±5% resistance=220 package="0603 [SMD]"]
  R2 = Resistor [tolerance=±5% resistance=220 package="0603 [SMD]"]
  R3 = Resistor [tolerance=±5% resistance=220 package="0603 [SMD]"]
  I2C[OLED] = Grove OLED 128x96
  M1 = ESP32-S3-DevKitC-1-N8R8-v1 [part_number=ESP32-S3-DevKitC-1-N8R8-v1]

nets:
  VIN: MAX30102_Sensor1.VIN, A1.Pin_3, A1.Pin_4, I2C[OLED].VCC, M1.pin_21
  N1: MAX30102_Sensor1.SCL, M1.pin_11
  N2: MAX30102_Sensor1.SDA, M1.pin_12
  GND: MAX30102_Sensor1.GND, A1.Pin_1, A1.Pin_2, R1.Pin_1, R2.Pin_0, R3.Pin_0, I2C[OLED].GND, M1.pin_22, M1.pin_24, M1.pin_44
  N3: SG1.1, R1.Pin_0
  N4: SG1.2, M1.pin_19
  N5: LED1.cathode, R2.Pin_1
  N6: LED1.anode, M1.pin_34
  N7: LED2.cathode, R3.Pin_1
  N8: LED2.anode, M1.pin_39
  N9: I2C[OLED].SDA, M1.pin_8
  N10: I2C[OLED].SCL, M1.pin_9

custom parts:
  MAX30102 Oximeter and Heart-Rate Sensor: The MAX30102 is an integrated pulse oximetry and heart-rate monitor biosensor module. It includes internal LEDs, photodetectors, optical elements, and low-noise electronics with ambient light rejection. The MAX30102 operates on a single 1.8V power supply and a separate 3.3V power supply for the internal LEDs. Communication is through a I2C-compatible interface.
  usbc to 12V module: usbc to 12V module.
  ESP32-S3-DevKitC-1-N8R8-v1: ESP32-S3-DevKitC-1-N8R8-v1 This module is 44pins long (2x22) and 11 pins width.
