# Fritzing sketch schematic_ftizing (saved by Fritzing 0.9.3b)
breadboards: 1

parts:
  S1 = 0.91 inch OLED I2C Display 128 x 32 Pixels
  M1 = ESP32-S3-DevKitC-1-N8R8-v1 [part_number=ESP32-S3-DevKitC-1-N8R8-v1]
  MAX30102_Sensor1 = MAX30102 Oximeter and Heart-Rate Sensor [part_number=MAX30102]  # not connected
  LED1 = smd LED [color="Red (635nm)" package="0805 [SMD]"]  # not connected
  LED2 = smd LED [color="Green (560nm)" package="0805 [SMD]"]  # not connected
  SG1 = Buzzer 12mm [package=buzzer-12mm]  # not connected
  A1 = usbc to 12V module
  R1 = Resistor [tolerance=±5% resistance=220 package=THT]
  R2 = Resistor [tolerance=±5% resistance=220 package="2512 [SMD]"]
  R3 = Resistor [tolerance=±5% resistance=220 package="2512 [SMD]"]

nets:
  N1: S1.VCC, M1.pin_21, A1.Pin_3, A1.Pin_4
  N2: S1.GND, M1.pin_22, M1.pin_24, A1.Pin_1, R1.Pin_0, R2.Pin_0, R3.Pin_0
  N3: S1.SDA, M1.pin_9
  N4: S1.SCL, M1.pin_8

custom parts:
  ESP32-S3-DevKitC-1-N8R8-v1: ESP32-S3-DevKitC-1-N8R8-v1 This module is 44pins long (2x22) and 11 pins width.
  MAX30102 Oximeter and Heart-Rate Sensor: The MAX30102 is an integrated pulse oximetry and heart-rate monitor biosensor module. It includes internal LEDs, photodetectors, optical elements, and low-noise electronics with ambient light rejection. The MAX30102 operates on a single 1.8V power supply and a separate 3.3V power supply for the internal LEDs. Communication is through a I2C-compatible interface.
  usbc to 12V module: usbc to 12V module.
